# Fritzing sketch Wall meter (saved by Fritzing 0.9.4)
breadboards: 1

parts:
  Part1 = Arduino Uno (Rev3)
  LED1 = LED - 5mm [color="Green (570nm)" package="5 mm [THT]"]  # not connected
  LED2 = LED - 5mm [color="Green (570nm)" package="5 mm [THT]"]  # not connected
  LED3 = LED - 5mm [color="Yellow (595nm)" package="5 mm [THT]"]  # not connected
  LED4 = LED - 5mm [color="Yellow (595nm)" package="5 mm [THT]"]  # not connected
  LED5 = LED - 5mm [color="Red (633nm)" package="5 mm [THT]"]  # not connected
  LED6 = LED - 5mm [color="Red (633nm)" package="5 mm [THT]"]  # not connected
  R1 = Resistor [tolerance=±5% resistance=330 package=THT]
  R2 = Resistor [tolerance=±5% resistance=330 package=THT]
  R3 = Resistor [tolerance=±5% resistance=330 package=THT]
  R4 = Resistor [tolerance=±5% resistance=330 package=THT]
  R5 = Resistor [tolerance=±5% resistance=330 package=THT]
  R6 = Resistor [tolerance=±5% resistance=330 package=THT]
  R7 = Photocell (LDR) [package=THT]
  R8 = Resistor [tolerance=±5% resistance=10k package=THT]
  C1 = Electrolytic Capacitor [capacitance=1µF package="100 mil [THT, electrolytic]"]
  R9 = Resistor [tolerance=±5% resistance=220 package=THT]
  R10 = Resistor [tolerance=±5% resistance=10k package=THT]
  D1 = Rectifier Diode [part_number=1N4001 package="300 mil [THT]"]
  LED7 = LED - 5mm [color="White (4500K)" package="5 mm [THT]"]  # not connected
  R11 = Resistor [tolerance=±5% resistance=330 package=THT]
  J1 = female pin header, 2 pins [form="♀ (female)"]
  J2 = female pin header, 2 pins [form="♀ (female)"]

nets:
  N1: Part1.A0, R6.Pin_0
  N2: Part1.A1, R9.Pin_0, D1.cathode
  N3: Part1.A2, R7.pin_0, R8.Pin_1
  N4: Part1.D8, R3.Pin_1
  N5: Part1.D9_PWM, R2.Pin_1
  N6: Part1.D10_PWM/SS, R1.Pin_1
  N7: Part1.D11_PWM/MOSI, R11.Pin_1
  N8: Part1.GND, R7.pin_1, C1.-, J1.pin1, J1.pin2
  N9: Part1.D2, D1.anode
  N10: Part1.D3_PWM, R8.Pin_0
  N11: Part1.D5_PWM, R6.Pin_1
  N12: Part1.D6_PWM, R5.Pin_1
  N13: Part1.D7, R4.Pin_1
  N14: C1.+, R9.Pin_1, R10.Pin_1
  N15: R10.Pin_0, J2.pin2
